// Logisim project my_CPU.circ as structural Verilog
module main (
  output [4:0] out_1
);

  wire B, CLK, IL, IR, J_jal, J_jalr, O_branch, OE_RAM, R, S, S_i_s_IMM, S_pc_reg, S_r_i, S_ram_reg, U_auipc,
       U_lui, WE_A_ALU, WE_A_op_B, WE_B_ALU, WE_GRG, WE_IR, WE_MA, WE_MD, WE_PC, WE_PCA4, WE_RAM;
  wire [1:0] S_in_GRG, S_in_PC, S_r12d, S_ujb_IMM;
  wire [2:0] funct3;
  wire [3:0] op_ALU;
  wire [4:0] instruction_stuct_decoder_1_rd, instruction_stuct_decoder_1_rs1, instruction_stuct_decoder_1_rs2;
  wire [6:0] funct7, opcode;
  wire [31:0] A_RAM, adder_1_out, adder_2_out, adder_3_out, adder_4_out, adder_5_out, alu_complete_1_out_4,
       I_RAM, imm_B, imm_I, imm_J, imm_S, imm_U, IR_q, multiplexer_1_out, multiplexer_2_out,
       multiplexer_4_out, multiplexer_5_out, multiplexer_6_out, multiplexer_7_out, multiplexer_8_out,
       not_1_out, O_A_ALU, O_B_ALU, O_GRG, O_RAM, pc_reset_val, PC_val, PCA4, register_3_q;

  Multiplexer #(.select(2), .width(32)) multiplexer_1 (
    .in0({32{1'b0}}), .in1(imm_U), .in2(imm_J), .in3(multiplexer_2_out), .out(multiplexer_1_out),
    .sel(S_ujb_IMM));
  Adder #(.width(32)) adder_1 (.a(PC_val), .b(32'h4), .out(adder_1_out));  // open: cin, cout
  Adder #(.width(32)) adder_2 (.a(PC_val), .b(multiplexer_1_out), .out(adder_2_out));  // open: cin, cout
  instruction_stuct_decoder instruction_stuct_decoder_1 (
    .instruction(IR_q), .opcode(opcode), .rd(instruction_stuct_decoder_1_rd),
    .rs1(instruction_stuct_decoder_1_rs1), .rs2(instruction_stuct_decoder_1_rs2), .funct3(funct3),
    .funct7(funct7), .I_11_0(imm_I), .S_11_0(imm_S), .B_12_1_0(imm_B), .U_31_12(imm_U), .J_20_1_0(imm_J));
  Multiplexer #(.width(32)) multiplexer_2 (.in0(32'h4), .in1(imm_B), .out(multiplexer_2_out), .sel(O_branch));
  Multiplexer #(.select(2), .width(5)) multiplexer_3 (
    .in1(instruction_stuct_decoder_1_rs1), .in2(instruction_stuct_decoder_1_rs2),
    .in3(instruction_stuct_decoder_1_rd), .out(out_1), .sel(S_r12d));  // open: in0
  decoder_opcode decoder_opcode_1 (
    .opcode(opcode), .R(R), .I_R(IR), .B(B), .I_L(IL), .S(S), .J_jal(J_jal), .J_jalr(J_jalr), .U_lui(U_lui),
    .U_auipc(U_auipc));
  PC_complete pc_complete_1 (
    .input_plus_1(adder_1_out), .input_plus_n(adder_2_out), .input_reset(pc_reset_val),
    .select_input(S_in_PC), .Write_enable(WE_PC), .Clock(CLK), .Pc_val(PC_val));  // open: in_4
  Multiplexer #(.select(2), .width(32)) multiplexer_4 (
    .in0(register_3_q), .in1(I_RAM), .in2(imm_U), .in3(PCA4), .out(multiplexer_4_out), .sel(S_in_GRG));
  Register #(.width(32)) MA (.D(multiplexer_6_out), .en(WE_MA), .clk(CLK), .Q(A_RAM));  // open: clr
  Multiplexer #(.width(32)) multiplexer_5 (.in0(imm_I), .in1(imm_S), .out(multiplexer_5_out), .sel(S_i_s_IMM));
  Multiplexer #(.width(32)) multiplexer_6 (.in0(PC_val), .in1(adder_3_out), .out(multiplexer_6_out), .sel(S_pc_reg));
  Adder #(.width(32)) adder_3 (.a(multiplexer_5_out), .b(O_GRG), .out(adder_3_out));  // open: cin, cout
  general_register_group general_register_group_1 (
    .Address_5_bit(out_1), .Write_enbale(WE_GRG), .Output_enable(1'b1), .Clock(CLK),
    .Data_input(multiplexer_4_out), .Data_output(O_GRG));
  Multiplexer #(.width(32)) multiplexer_7 (.in0(O_RAM), .in1(O_GRG), .out(multiplexer_7_out), .sel(S_ram_reg));
  Register #(.width(32)) MD (.D(multiplexer_7_out), .en(WE_MD), .clk(CLK), .Q(I_RAM));  // open: clr
  Register #(.width(32)) u_IR (.D(I_RAM), .en(WE_IR), .clk(CLK), .Q(IR_q));  // open: clr
  Multiplexer #(.width(32)) multiplexer_8 (.in0(O_GRG), .in1(imm_I), .out(multiplexer_8_out), .sel(S_r_i));
  Register #(.width(32)) register_1 (.D(O_GRG), .en(WE_A_ALU), .clk(CLK), .Q(O_A_ALU));  // open: clr
  Register #(.width(32)) register_2 (.D(multiplexer_8_out), .en(WE_B_ALU), .clk(CLK), .Q(O_B_ALU));  // open: clr
  Register #(.width(32)) PC_A4 (.D(adder_4_out), .en(WE_PCA4), .clk(CLK), .Q(PCA4));  // open: clr
  Adder #(.width(32)) adder_4 (.a(PC_val), .b(32'h4), .out(adder_4_out));  // open: cin, cout
  Adder #(.width(32)) adder_5 (.a(imm_I), .b(O_GRG), .out(adder_5_out));  // open: cin, cout
  assign not_1_out = ~32'h1;  // NOT_Gate not_1, 32 bits wide
  assign pc_reset_val = adder_5_out & not_1_out;  // AND_Gate and_1, 32 bits wide
  encoder_4_2 encoder_4_2_1 (.i3(B), .i2(J_jal), .i1(U_auipc), .o1(S_ujb_IMM[1]), .o0(S_ujb_IMM[0]));  // open: i0
  B_type_instruction_complete b_type_instruction_complete_1 (
    .rs1(O_A_ALU), .rs2(O_B_ALU), .funct3(funct3), .opcode(opcode), .Branch(O_branch));
  ALU_complete alu_complete_1 (.A(O_A_ALU), .B(O_B_ALU), .op(op_ALU), .out_4(alu_complete_1_out_4));
  Register #(.width(32)) register_3 (
    .D(alu_complete_1_out_4), .en(WE_A_op_B), .clk(CLK), .Q(register_3_q));  // open: clr
  RAM #(.addrWidth(24), .dataWidth(32)) ram_1 (
    .addr(A_RAM[23:0]), .we(WE_RAM), .oe(OE_RAM), .clk(CLK), .din(I_RAM), .dout(O_RAM));

  // Other names for the same wires on the sheet: O_MD[31:0] = I_RAM
endmodule

module PC (
  input  [31:0] Pc_input,
  input  Write_enable,
  input  Clock,
  output [31:0] Pc_ouput
);

  Register #(.width(32)) register_1 (.D(Pc_input), .en(Write_enable), .clk(Clock), .Q(Pc_ouput));  // open: clr
endmodule

module PC_complete (
  input  [31:0] input_plus_1,
  input  [31:0] input_plus_n,
  input  [31:0] input_reset,
  input  [31:0] in_4,
  input  [1:0] select_input,
  input  Write_enable,
  input  Clock,
  output [31:0] Pc_val
);

  wire [31:0] multiplexer_1_out;

  Multiplexer #(.select(2), .width(32)) multiplexer_1 (
    .in0(input_plus_1), .in1(input_plus_n), .in2(input_reset), .in3(in_4), .out(multiplexer_1_out),
    .sel(select_input));
  PC pc_1 (.Pc_input(multiplexer_1_out), .Write_enable(Write_enable), .Clock(Clock), .Pc_ouput(Pc_val));
endmodule

module ALU (
  input  [31:0] A,
  input  [31:0] B,
  output [31:0] Carry,
  output [31:0] add,
  output [31:0] Borrow,
  output [31:0] subtract,
  output [31:0] shift_left_logic,
  output [31:0] shift_right_logic,
  output [31:0] shift_right_arithmetic,
  output [31:0] A_and_B,
  output [31:0] A_or_B,
  output [31:0] A_xor_B,
  output [31:0] slt,
  output [31:0] sltu
);

  wire adder_1_cout, comparator_1_lt, comparator_2_lt, subtractor_1_bout;

  Adder #(.width(32)) adder_1 (.a(A), .b(B), .out(add), .cin(1'b0), .cout(adder_1_cout));
  Subtractor #(.width(32)) subtractor_1 (.a(A), .b(B), .out(subtract), .bin(1'b0), .bout(subtractor_1_bout));
  Shifter #(.width(32)) shifter_1 (.in(A), .\dist (B[4:0]), .out(shift_left_logic));
  Shifter #(.shift("lr"), .width(32)) shifter_2 (.in(A), .\dist (B[4:0]), .out(shift_right_logic));
  Shifter #(.shift("ar"), .width(32)) shifter_3 (.in(A), .\dist (B[4:0]), .out(shift_right_arithmetic));
  assign A_and_B = A & B;  // AND_Gate and_1, 32 bits wide
  assign A_or_B = A | B;  // OR_Gate or_1, 32 bits wide
  assign A_xor_B = A ^ B;  // XOR_Gate xor_1, 32 bits wide
  Comparator #(.width(32)) comparator_1 (.a(A), .b(B), .lt(comparator_1_lt));  // open: gt, eq
  Comparator #(.mode("unsigned"), .width(32)) comparator_2 (.a(A), .b(B), .lt(comparator_2_lt));  // open: gt, eq
  Multiplexer #(.width(32)) multiplexer_1 (.in0({32{1'b0}}), .in1(32'h1), .out(Carry), .sel(adder_1_cout));
  Multiplexer #(.width(32)) multiplexer_2 (.in0({32{1'b0}}), .in1(32'h1), .out(Borrow), .sel(subtractor_1_bout));
  Multiplexer #(.width(32)) multiplexer_3 (.in0({32{1'b0}}), .in1(32'h1), .out(slt), .sel(comparator_1_lt));
  Multiplexer #(.width(32)) multiplexer_4 (.in0({32{1'b0}}), .in1(32'h1), .out(sltu), .sel(comparator_2_lt));
endmodule

module ALU_complete (
  input  [31:0] A,
  input  [31:0] B,
  input  [3:0] op,
  output [31:0] out_4
);

  wire decoder_1_out0, decoder_1_out1, decoder_1_out2, decoder_1_out3, decoder_1_out4, decoder_1_out5,
       decoder_1_out6, decoder_1_out7, decoder_1_out8, decoder_1_out9;
  wire [31:0] alu_1_a_and_b, alu_1_a_or_b, alu_1_a_xor_b, alu_1_add, alu_1_shift_left_logic,
       alu_1_shift_right_arithmetic, alu_1_shift_right_logic, alu_1_slt, alu_1_sltu, alu_1_subtract;

  Decoder #(.enable("false"), .select(4)) decoder_1 (
    .out0(decoder_1_out0), .out1(decoder_1_out1), .out2(decoder_1_out2), .out3(decoder_1_out3),
    .out4(decoder_1_out4), .out5(decoder_1_out5), .out6(decoder_1_out6), .out7(decoder_1_out7),
    .out8(decoder_1_out8), .out9(decoder_1_out9), .sel(op));  // open: out10, out11, out12, out13, out14, out15
  ALU alu_1 (
    .A(A), .B(B), .add(alu_1_add), .subtract(alu_1_subtract), .shift_left_logic(alu_1_shift_left_logic),
    .shift_right_logic(alu_1_shift_right_logic), .shift_right_arithmetic(alu_1_shift_right_arithmetic),
    .A_and_B(alu_1_a_and_b), .A_or_B(alu_1_a_or_b), .A_xor_B(alu_1_a_xor_b), .slt(alu_1_slt),
    .sltu(alu_1_sltu));  // open: Carry, Borrow
  assign out_4 = decoder_1_out9 ? alu_1_sltu : 32'bz;  // Controlled_Buffer controlled_buffer_1
  assign out_4 = decoder_1_out5 ? alu_1_a_and_b : 32'bz;  // Controlled_Buffer controlled_buffer_2
  assign out_4 = decoder_1_out6 ? alu_1_a_or_b : 32'bz;  // Controlled_Buffer controlled_buffer_3
  assign out_4 = decoder_1_out7 ? alu_1_a_xor_b : 32'bz;  // Controlled_Buffer controlled_buffer_4
  assign out_4 = decoder_1_out8 ? alu_1_slt : 32'bz;  // Controlled_Buffer controlled_buffer_5
  assign out_4 = decoder_1_out2 ? alu_1_shift_left_logic : 32'bz;  // Controlled_Buffer controlled_buffer_6
  assign out_4 = decoder_1_out3 ? alu_1_shift_right_logic : 32'bz;  // Controlled_Buffer controlled_buffer_7
  assign out_4 = decoder_1_out4 ? alu_1_shift_right_arithmetic : 32'bz;  // Controlled_Buffer controlled_buffer_8
  assign out_4 = decoder_1_out0 ? alu_1_add : 32'bz;  // Controlled_Buffer controlled_buffer_9
  assign out_4 = decoder_1_out1 ? alu_1_subtract : 32'bz;  // Controlled_Buffer controlled_buffer_10
endmodule

module general_register_group (
  input  [4:0] Address_5_bit,
  input  Write_enbale,
  input  Output_enable,
  input  Clock,
  input  [31:0] Data_input,
  output [31:0] Data_output
);

  RAM #(.addrWidth(5), .asyncread("true"), .dataWidth(32)) Register_group (
    .addr(Address_5_bit), .we(Write_enbale), .oe(Output_enable), .clk(Clock), .din(Data_input),
    .dout(Data_output));
endmodule

module instruction_stuct_decoder (
  input  [31:0] instruction,
  output [6:0] opcode,
  output [4:0] rd,
  output [4:0] rs1,
  output [4:0] rs2,
  output [2:0] funct3,
  output [6:0] funct7,
  output [31:0] I_11_0,
  output [31:0] S_11_0,
  output [31:0] B_12_1_0,
  output [31:0] U_31_12,
  output [31:0] J_20_1_0
);

  wire [31:0] bit_extender_1_out;

  assign bit_extender_1_out = {{12{instruction[31]}}, instruction[31:12]};  // Bit_Extender bit_extender_1
  assign I_11_0 = {{20{instruction[31]}}, instruction[31:20]};  // Bit_Extender bit_extender_2
  assign S_11_0 = {{20{instruction[31]}}, {instruction[31:25], instruction[11:7]}};  // Bit_Extender bit_extender_3
  assign B_12_1_0 = {{19{instruction[31]}}, {instruction[31], instruction[7], instruction[30:25], instruction[11:8], 1'b0}};  // Bit_Extender bit_extender_4
  Shifter #(.width(32)) shifter_1 (.in(bit_extender_1_out), .\dist (5'b01100), .out(U_31_12));
  assign J_20_1_0 = {{11{instruction[31]}}, {instruction[31], instruction[19:12], instruction[20], instruction[30:21], 1'b0}};  // Bit_Extender bit_extender_5

  assign funct3 = instruction[14:12];
  assign funct7 = instruction[31:25];
  assign opcode = instruction[6:0];
  assign rd = instruction[11:7];
  assign rs1 = instruction[19:15];
  assign rs2 = instruction[24:20];
endmodule

module decoder_opcode (
  input  [6:0] opcode,
  output R,
  output I_R,
  output B,
  output I_L,
  output S,
  output J_jal,
  output J_jalr,
  output U_lui,
  output U_auipc
);

  Comparator #(.mode("unsigned"), .width(7)) comparator_1 (.a(opcode), .b(7'b0110011), .eq(R));  // open: gt, lt
  Comparator #(.mode("unsigned"), .width(7)) comparator_2 (.a(opcode), .b(7'b0010011), .eq(I_R));  // open: gt, lt
  Comparator #(.mode("unsigned"), .width(7)) comparator_3 (.a(opcode), .b(7'b1100011), .eq(B));  // open: gt, lt
  Comparator #(.mode("unsigned"), .width(7)) comparator_4 (.a(opcode), .b(7'b0000011), .eq(I_L));  // open: gt, lt
  Comparator #(.mode("unsigned"), .width(7)) comparator_5 (.a(opcode), .b(7'b0100011), .eq(S));  // open: gt, lt
  Comparator #(.mode("unsigned"), .width(7)) comparator_6 (.a(opcode), .b(7'b1101111), .eq(J_jal));  // open: gt, lt
  Comparator #(.mode("unsigned"), .width(7)) comparator_7 (.a(opcode), .b(7'b1100111), .eq(J_jalr));  // open: gt, lt
  Comparator #(.mode("unsigned"), .width(7)) comparator_8 (.a(opcode), .b(7'b0110111), .eq(U_lui));  // open: gt, lt
  Comparator #(.mode("unsigned"), .width(7)) comparator_9 (.a(opcode), .b(7'b0010111), .eq(U_auipc));  // open: gt, lt
endmodule

module B_type_instruction (
  input  [31:0] rs1,
  input  [31:0] rs2,
  output beq,
  output bne,
  output blt,
  output bge,
  output bltu,
  output bgeu
);

  Comparator #(.width(32)) comparator_1 (.a(rs1), .b(rs2), .eq(beq), .lt(blt));  // open: gt
  Comparator #(.mode("unsigned"), .width(32)) comparator_2 (.a(rs1), .b(rs2), .lt(bltu));  // open: gt, eq
  not not_1 (bne, beq);
  not not_2 (bge, blt);
  not not_3 (bgeu, bltu);
endmodule

module B_type_instruction_complete (
  input  [31:0] rs1,
  input  [31:0] rs2,
  input  [2:0] funct3,
  input  [6:0] opcode,
  output Branch
);

  wire b_type_instruction_1_beq, b_type_instruction_1_bge, b_type_instruction_1_bgeu,
       b_type_instruction_1_blt, b_type_instruction_1_bltu, b_type_instruction_1_bne, comparator_1_eq,
       multiplexer_1_out;

  B_type_instruction b_type_instruction_1 (
    .rs1(rs1), .rs2(rs2), .beq(b_type_instruction_1_beq), .bne(b_type_instruction_1_bne),
    .blt(b_type_instruction_1_blt), .bge(b_type_instruction_1_bge), .bltu(b_type_instruction_1_bltu),
    .bgeu(b_type_instruction_1_bgeu));
  Comparator #(.mode("unsigned"), .width(7)) comparator_1 (
    .a(opcode), .b(7'b1100011), .eq(comparator_1_eq));  // open: gt, lt
  Multiplexer #(.select(3)) multiplexer_1 (
    .in0(b_type_instruction_1_beq), .in1(b_type_instruction_1_bne), .in4(b_type_instruction_1_blt),
    .in5(b_type_instruction_1_bge), .in6(b_type_instruction_1_bltu), .in7(b_type_instruction_1_bgeu),
    .out(multiplexer_1_out), .sel(funct3));  // open: in2, in3
  and and_1 (Branch, multiplexer_1_out, comparator_1_eq);
endmodule

module encoder_4_2 (
  input  i3,
  input  i2,
  input  i1,
  input  i0,
  output o1,
  output o0
);

  wire and_1_out, and_2_out, and_3_out, and_4_out, not_1_out, not_2_out, not_3_out, not_4_out;

  not not_1 (not_1_out, i3);
  not not_2 (not_2_out, i2);
  not not_3 (not_3_out, i1);
  not not_4 (not_4_out, i0);
  and and_1 (and_1_out, not_1_out, i2, not_3_out, not_4_out);
  and and_2 (and_2_out, i3, not_2_out, not_3_out, not_4_out);
  and and_3 (and_3_out, not_1_out, not_2_out, i1, not_4_out);
  and and_4 (and_4_out, i3, not_2_out, not_3_out, not_4_out);
  or or_1 (o1, and_1_out, and_2_out);
  or or_2 (o0, and_3_out, and_4_out);
endmodule
